# Fritzing sketch emogenation-electronic sketch (saved by Fritzing 0.9.3b)
stripboards: 1

parts:
  Part1 = Arduino Uno (Rev3)
  Part2 = Bluetooth HC-05 Macho
  R1 = Resistor [tolerance=±5% resistance=220 package=THT]
  R2 = Resistor [tolerance=±5% resistance=220 package=THT]
  R3 = Resistor [tolerance=±5% resistance=220 package=THT]
  R4 = Resistor [tolerance=±5% resistance=220 package=THT]
  R5 = Resistor [tolerance=±5% resistance=220 package=THT]
  S1 = Pushbutton [package=THT]
  S2 = Pushbutton [package=THT]
  S3 = Pushbutton [package=THT]
  S4 = Pushbutton [package=THT]
  S5 = Pushbutton [package=THT]
  R6 = Resistor [tolerance=±5% resistance=220 package=THT]
  R7 = Resistor [tolerance=±5% resistance=220 package=THT]
  R8 = Resistor [tolerance=±5% resistance=220 package=THT]
  R10 = Resistor [tolerance=±5% resistance=220 package=THT]
  LED2 = RGB LED (com. cathode, rgb) [package="5 mm [THT]"]
  R9 = Resistor [tolerance=±5% resistance=220 package=THT]
  LED3 = RGB LED (com. cathode, rgb) [package="5 mm [THT]"]
  LED4 = RGB LED (com. cathode, rgb) [package="5 mm [THT]"]
  LED5 = RGB LED (com. cathode, rgb) [package="5 mm [THT]"]
  LED6 = RGB LED (com. cathode, rgb) [package="5 mm [THT]"]

nets:
  N1: Part1.A1, S5.leg1
  N2: Part1.A2, S3.leg1
  N3: Part1.A3, S1.leg1
  N4: Part1.A4/SDA, S2.leg1
  N5: Part1.A5/SCL, S4.leg1
  N6: Part1.D8, R2.Pin_0
  N7: Part1.D9_PWM, R1.Pin_0
  N8: Part1.D10_PWM/SS, Part2.RXD
  N9: Part1.D11_PWM/MOSI, Part2.TXD
  N10: Part1.D12/MISO, R8.Pin_0
  N11: Part1.D13/SCK, R9.Pin_0
  N12: Part1.D2, R10.Pin_0
  N13: Part1.D3_PWM, R7.Pin_0
  N14: Part1.D4, R5.Pin_0
  N15: Part1.D5_PWM, R6.Pin_0
  N16: Part1.D6_PWM, R4.Pin_0
  N17: Part1.D7, R3.Pin_0
  5V: Part1.5V, Part2.VCC, S1.leg0, S2.leg0, S3.leg0, S4.leg0, S5.leg0
  GND: Part1.GND, Part2.GND, LED2.common_cathode, LED3.common_cathode, LED4.common_cathode, LED5.common_cathode, LED6.common_cathode

// code stored in the sketch: emogenation.ino

#include <SoftwareSerial.h>

SoftwareSerial btSerial(10, 11); // RX, TX
int LED_R_G[5][2] = {{12,13}, {8,9}, {6,7}, {5,4}, {2,3}};
int BUTTON[5] = {A1, A2, A3, A4, A5};
int previousBtnState[5] = {LOW, LOW, LOW, LOW, LOW};


void setup() {
  Serial.begin(9600);
  btSerial.begin(9600);

  // Button lines are set to OUTPUT since these are analog lines
  for (int i=0; i<5; i++)
    pinMode(BUTTON[i], OUTPUT);
  
  for (int i=0; i<5; i++) {
    pinMode(LED_R_G[i][0], OUTPUT); // R line
    pinMode(LED_R_G[i][1], OUTPUT); // G line
  }
}

void loop() {
  int ledNumber;
  // test 5 time the commands in case all 5 leds got command
  for (int i=0;i<5;i++) {
    if (btSerial.available()) {
      int asciiValue = btSerial.read();
      // validate that an ascii representing led valid number between 1-5
      ledNumber = asciiValue - '0';
      if (ledNumber < 0 || ledNumber > 4) {
        Serial.println(" ERROR in receiving BT info. Illegal ledNumber.");
        continue;  
      } else {  

        if (btSerial.available()) {
          int ledCommand = btSerial.read();
          switch (ledCommand) {
            case 'R' :
              digitalWrite(LED_R_G[ledNumber][0], HIGH);
              digitalWrite(LED_R_G[ledNumber][1], LOW);
              break;
            case 'G' :
              digitalWrite(LED_R_G[ledNumber][0], LOW);
              digitalWrite(LED_R_G[ledNumber][1], HIGH);
              break;
            case '0' :
              digitalWrite(LED_R_G[ledNumber][0], LOW);
              digitalWrite(LED_R_G[ledNumber][1], LOW);
              break;
            default:
              //illegal value
              Serial.println("ERROR in receiving BT info. Illegal ledCommand");
              
          }
        }
      }
    }
  }

  // handle buttons state 
  // send only button number when pressed (like onClick() )
  int currentButtonState;
  for (int i=0; i<5; i++) {
      currentButtonState = digitalRead(BUTTON[i]);
      if (currentButtonState != previousBtnState[i]) { //change in state
        if (currentButtonState == HIGH) {
          char value = '0'+i;
          btSerial.println(value); // send the ascii of the pressed button
          Serial.print(value); // send the ascii of the pressed button
        }
        previousBtnState[i] = currentButtonState;
      }
  }

  delay(30);        // delay in between reads for stability     
}
